# Fritzing sketch brew_temp_v1 (saved by Fritzing 0.8.3b)
breadboards: 1
stripboards: 1

parts:
  Part1 = Arduino Uno (Rev3)
  LCD1 = LCD screen
  R1 = Trimmer Potentiometer [maximum_resistance=10kΩ package=THT]
  LCD2 = LCD screen
  R2 = Trimmer Potentiometer [maximum_resistance=10kΩ package=THT]

nets:
  GND: Part1.GND, LCD2.VSS, LCD2.R/W, LCD2.LED-, R2.leg1, R2.leg2
  N1: Part1.D8, LCD2.DB6
  N2: Part1.D9_PWM, LCD2.DB7
  N3: Part1.D4, LCD2.RS
  N4: Part1.D5_PWM, LCD2.E
  N5: Part1.D6_PWM, LCD2.DB4
  N6: Part1.D7, LCD2.DB5
  5V: Part1.5V, LCD2.VDD, LCD2.LED+
  N7: LCD1.VSS, LCD1.R/W, LCD1.LED-, R1.leg1, R1.leg2
  N8: LCD1.VDD, LCD1.LED+
  N9: LCD1.V0, R1.wiper
  N10: LCD2.V0, R2.wiper
